# Fritzing sketch distance-measurement-v-1_0 (saved by Fritzing 0.9.3b)

parts:
  Part1 = Arduino Uno (Rev3)
  hc-sr1 = hc-sr04

nets:
  N1: Part1.D11_PWM/MOSI, hc-sr1.Echo
  N2: Part1.D12/MISO, hc-sr1.Trig
  5V: Part1.5V, hc-sr1.VCC
  GND: Part1.GND, hc-sr1.GND
