# Fritzing sketch imu-v-1_0 (saved by Fritzing 0.9.3b)
breadboards: 1

parts:
  Part1 = InvenSense MPU6050
  LCD1 = LCD screen
  R1 = TRIMPOT [package=trimpot-3mm-2]
  Part2 = Arduino Uno (Rev3) - ICSP
  R3 = Resistor [tolerance=±1% resistance=220 package=THT]

nets:
  VCC: Part1.VCC, LCD1.VDD, R1.CCW, Part2.5V, R3.Pin_0
  GND: Part1.GND, Part1.INT, LCD1.VSS, LCD1.R/W, LCD1.LED-, R1.WIPER, Part2.GND
  N1: Part1.SCL, Part2.A5/SCL
  N2: Part1.SDA, Part2.A4/SDA
  N3: LCD1.V0, R1.CW
  N4: LCD1.RS, Part2.ICSP_MISO, Part2.D12/MISO
  N5: LCD1.E, Part2.D11_PWM/MOSI
  N6: LCD1.DB4, Part2.D5_PWM
  N7: LCD1.DB5, Part2.D4
  N8: LCD1.DB6, Part2.D3_PWM
  N9: LCD1.DB7, Part2.D2
  N10: LCD1.LED+, R3.Pin_1
