# Fritzing sketch infrared-send-receive-v-1_0 (saved by Fritzing 0.9.3b)

parts:
  Part2 = IR Receiver Breakout [package=PCB]
  Part3 = Arduino Uno (Rev3) - ICSP

nets:
  GND: Part2.GND, Part3.GND
  N1: Part2.OUT, Part3.5V
  N2: Part2.VCC, Part3.D11_PWM/MOSI
