# Fritzing sketch membran-keypad-v-1_0 (saved by Fritzing 0.9.3b)

parts:
  Keypad4x1 = Keypad Membran 4x4
  Part1 = Arduino Uno (Rev3)

nets:
  N1: Keypad4x1.Pin1, Part1.D9_PWM
  N2: Keypad4x1.Pin2, Part1.D8
  N3: Keypad4x1.Pin3, Part1.D7
  N4: Keypad4x1.Pin4, Part1.D6_PWM
  N5: Keypad4x1.Pin5, Part1.D5_PWM
  N6: Keypad4x1.Pin6, Part1.D4
  N7: Keypad4x1.Pin7, Part1.D3_PWM
  N8: Keypad4x1.Pin8, Part1.D2

custom parts:
  Keypad Membran 4x4: Membrane Keypad 4x4 Matrix
