# Fritzing sketch pir-v-1_0 (saved by Fritzing 0.9.3b)
breadboards: 1

parts:
  LCD1 = LCD screen
  R1 = TRIMPOT [package=trimpot-3mm-2]
  Part2 = Arduino Uno (Rev3) - ICSP
  R3 = Resistor [tolerance=±1% resistance=220 package=THT]
  Part3 = HC-SR501 Body Sensor Module

nets:
  GND: LCD1.VSS, LCD1.R/W, LCD1.LED-, R1.WIPER, Part2.GND, Part3.GND
  VDD: LCD1.VDD, R1.CCW, Part2.5V, R3.Pin_0, Part3.VCC
  N1: LCD1.V0, R1.CW
  N2: LCD1.RS, Part2.ICSP_MISO, Part2.D12/MISO
  N3: LCD1.E, Part2.D11_PWM/MOSI
  N4: LCD1.DB4, Part2.D5_PWM
  N5: LCD1.DB5, Part2.D4
  N6: LCD1.DB6, Part2.D3_PWM
  N7: LCD1.DB7, Part2.D2
  N8: LCD1.LED+, R3.Pin_1
  N9: Part2.D7, Part3.OUT

custom parts:
  HC-SR501 Body Sensor Module: Pyroelectric Infrared PIR Motion Sensor Detector Module
