# Fritzing sketch rfid-v-1_0 (saved by Fritzing 0.9.3b)
breadboards: 1

parts:
  LCD1 = LCD screen
  R1 = TRIMPOT [package=trimpot-3mm-2]
  Part2 = Arduino Uno (Rev3) - ICSP
  R3 = Resistor [tolerance=±1% resistance=220 package=THT]
  Part3 = RFID-RC522-v2

nets:
  GND: LCD1.VSS, LCD1.R/W, LCD1.LED-, R1.WIPER, Part2.GND, Part3.GND
  VDD: LCD1.VDD, R1.CCW, Part2.5V, R3.Pin_0
  N1: LCD1.V0, R1.CW
  N2: LCD1.RS, Part2.D7
  N3: LCD1.E, Part2.D6_PWM
  N4: LCD1.DB4, Part2.D5_PWM
  N5: LCD1.DB5, Part2.D4
  N6: LCD1.DB6, Part2.D3_PWM
  N7: LCD1.DB7, Part2.D2
  N8: LCD1.LED+, R3.Pin_1
  N9: Part2.D9_PWM, Part3.RST
  N10: Part2.D10_PWM/SS, Part3.SDA
  N11: Part2.D11_PWM/MOSI, Part3.MOSI
  N12: Part2.D12/MISO, Part3.MISO
  N13: Part2.D13/SCK, Part3.SCK
  3V3: Part2.3V3, Part3.3.3V

custom parts:
  RFID-RC522-v2: A simple China made RFID-RC522 Reader; do check the pin labels, as this is a MFRC522 based clone.
