# Fritzing sketch rtc-v-1_0 (saved by Fritzing 0.9.3b)
breadboards: 1

parts:
  LCD1 = LCD screen
  Part2 = Arduino Uno (Rev3) - ICSP
  R1 = Resistor [tolerance=±1% resistance=220 package=THT]
  S1 = Momentary Switch [package=ksa_sealed_tac_switch]
  S2 = Momentary Switch [package=ksa_sealed_tac_switch]
  S3 = Momentary Switch [package=ksa_sealed_tac_switch]
  ZS-042_RTC1 = ZS-042 RTC Module
  R1_2 = TRIMPOT [package=trimpot-3mm-2]
  R1_3 = TRIMPOT [package=trimpot-3mm-2]

nets:
  GND: LCD1.VSS, LCD1.R/W, LCD1.LED-, Part2.GND, S1.1, S1.2, S2.1, S2.2, S3.1, S3.2, ZS-042_RTC1.GND, R1_2.WIPER, R1_3.WIPER
  VDD: LCD1.VDD, Part2.5V, R1.Pin_0, ZS-042_RTC1.VCC, R1_2.CCW, R1_3.CCW
  N1: LCD1.V0, R1_2.CW
  N2: LCD1.RS, Part2.ICSP_MISO, Part2.D12/MISO
  N3: LCD1.E, Part2.D11_PWM/MOSI
  N4: LCD1.DB4, Part2.D5_PWM
  N5: LCD1.DB5, Part2.D4
  N6: LCD1.DB6, Part2.D3_PWM
  N7: LCD1.DB7, Part2.D2
  N8: LCD1.LED+, R1.Pin_1
  N9: Part2.D13/SCK, S3.3, S3.4
  N10: Part2.A4/SDA, ZS-042_RTC1.SDA
  N11: Part2.A5/SCL, ZS-042_RTC1.SCL
  N12: Part2.D6_PWM, S2.3, S2.4
  N13: Part2.D7, S1.3, S1.4
