# Fritzing sketch simple-multi-tasking (saved by Fritzing 0.9.3b)
breadboards: 1

parts:
  Part1 = Arduino Uno (Rev3)
  LED1 = smd LED [color="Red (633nm)" package="1206 [SMD]"]
  R1 = Resistor [tolerance=±5% resistance=220 package="2010 [SMD]"]
  R2 = Resistor [tolerance=±5% resistance=220 package="2010 [SMD]"]
  LED2 = smd LED [color="Red (633nm)" package="1206 [SMD]"]
  J1 = Basic Servo

nets:
  N1: Part1.D10_PWM/SS, J1.pulse
  N2: Part1.D12/MISO, R2.Pin_1
  N3: Part1.D13/SCK, R1.Pin_1
  GND: Part1.GND, LED1.cathode, LED2.cathode, J1.gnd
  5V: Part1.5V, J1.vcc
  N4: LED1.anode, R1.Pin_0
  N5: R2.Pin_0, LED2.anode
