# Fritzing sketch sound-v-1_0 (saved by Fritzing 0.9.3b)
breadboards: 1

parts:
  Part1 = Arduino Uno (Rev3) - ICSP
  Decrease_Max_Noise = Pushbutton [package="[SMD]"]
  S2 = Pushbutton [package="[SMD]"]
  S3 = Pushbutton [package="[SMD]"]
  KY-037 = KY-038
  U1 = MAX7219 [package=dil24]

nets:
  N1: Part1.A0, KY-037.pin1
  N2: Part1.D10_PWM/SS, U1.CLK
  N3: Part1.D11_PWM/MOSI, U1.LOAD
  N4: Part1.D12/MISO, U1.DIN
  N5: Part1.D2, S3.Pin_3, S3.Pin_4
  N6: Part1.D3_PWM, S2.Pin_3, S2.Pin_4
  N7: Part1.D4, Decrease_Max_Noise.Pin_3, Decrease_Max_Noise.Pin_4
  5V: Part1.5V, KY-037.pin3, U1.VCC
  GND: Part1.GND, Decrease_Max_Noise.Pin_1, Decrease_Max_Noise.Pin_2, S2.Pin_1, S2.Pin_2, S3.Pin_1, S3.Pin_2, KY-037.pin2, U1.GND2

custom parts:
  KY-038: ky-038 Microphone sound sensor module
