# Fritzing sketch temperature-and-humidity-v-1_0 (saved by Fritzing 0.9.3b)

parts:
  Part1 = Arduino Uno (Rev3)
  DHT1 = DHT11 Humitidy and Temperature Sensor

nets:
  N1: Part1.D2, DHT1.DATA
  5V: Part1.5V, DHT1.VDD
  GND: Part1.GND, DHT1.GND

custom parts:
  DHT11 Humitidy and Temperature Sensor: DHT11 Humidity and Temperature Sensor
