# Fritzing sketch temperature-and-humidity-v-2_0 (saved by Fritzing 0.9.3b)
breadboards: 1

parts:
  Part1 = Arduino Uno (Rev3)
  DHT1 = DHT11 Humitidy and Temperature Sensor
  LCD1 = LCD screen
  R7 = Resistor [tolerance=±1% resistance=220 package=THT]
  R11 = TRIMPOT [package=trimpot-3mm-2]
  R13 = Resistor [tolerance=±1% resistance=10k package=THT]
  R14 = Temperature Sensor (Thermistor) [thermistor_type=NTC package=THT]

nets:
  N1: Part1.A0, R13.Pin_1, R14.pin_1
  N2: Part1.D8, DHT1.DATA
  N3: Part1.D2, LCD1.DB7
  N4: Part1.D3_PWM, LCD1.DB6
  N5: Part1.D4, LCD1.DB5
  N6: Part1.D5_PWM, LCD1.DB4
  N7: Part1.D6_PWM, LCD1.E
  N8: Part1.D7, LCD1.RS
  VDD: Part1.5V, DHT1.VDD, LCD1.VDD, R7.Pin_0, R11.CCW, R14.pin_0
  GND: Part1.GND, DHT1.GND, LCD1.VSS, LCD1.R/W, LCD1.LED-, R11.WIPER, R13.Pin_0
  N9: LCD1.V0, R11.CW
  N10: LCD1.LED+, R7.Pin_1

custom parts:
  DHT11 Humitidy and Temperature Sensor: DHT11 Humidity and Temperature Sensor
