# Fritzing sketch water-level-sensor-v-1_0 (saved by Fritzing 0.9.3b)

parts:
  Part1 = Arduino Uno (Rev3) - ICSP
  Water_Level_Sensor1 = Water Level Sensor

nets:
  N1: Part1.A0, Water_Level_Sensor1.SIG
  5V: Part1.5V, Water_Level_Sensor1.VCC
  GND: Part1.GND, Water_Level_Sensor1.GND

custom parts:
  Water Level Sensor: A water level sensor. This sensor operates at 3V to 5V. The Sig (signal) pin outputs an analogue signal that is in proportion to the amount of water in contact with the sensor.
